# Fritzing sketch dumpster-controller (saved by Fritzing 0.9.3b)
breadboards: 1

parts:
  Part1 = Arduino Uno (Rev3)
  Part2 = Bluetooth HC-05 Macho
  J1 = Basic Servo
  R1 = Resistor [tolerance=±5% resistance=220 package=THT]
  LED1 = LED - 5mm [color="Blue (525nm)" package="5 mm [THT]"]
  R2 = Resistor [tolerance=±5% resistance=220 package=THT]
  LED2 = LED - 5mm [color="Blue (525nm)" package="5 mm [THT]"]
  R3 = Resistor [tolerance=±5% resistance=220 package=THT]
  LED3 = LED - 5mm [color="Blue (525nm)" package="5 mm [THT]"]

nets:
  N1: Part1.D8, R2.Pin_1
  N2: Part1.D9_PWM, R3.Pin_1
  N3: Part1.D2, Part2.TXD
  N4: Part1.D3_PWM, Part2.RXD
  N5: Part1.D5_PWM, J1.pulse
  N6: Part1.D7, R1.Pin_1
  VCC: Part1.5V, Part2.VCC, J1.vcc
  GND: Part1.GND, Part2.GND, J1.gnd, LED1.cathode, LED2.cathode, LED3.cathode
  N7: R1.Pin_0, LED1.anode
  N8: R2.Pin_0, LED2.anode
  N9: R3.Pin_0, LED3.anode
