# Fritzing sketch dumpster-edge (saved by Fritzing 0.9.3b)
breadboards: 1

parts:
  U1 = NodeMCU V1.0
  R1 = Resistor [tolerance=±5% resistance=220 package=THT]
  LED2 = LED - 5mm [color="Red (633nm)" package="5 mm [THT]"]
  R2 = Resistor [tolerance=±5% resistance=220 package=THT]
  LED3 = LED - 5mm [color="Green (570nm)" package="5 mm [THT]"]
  R3 = Rotary Potentiometer (Small) [maximum_resistance=100kΩ package=THT]

nets:
  N1: U1.D0, R1.Pin_1
  N2: U1.D1, R2.Pin_1
  N3: U1.3V3, R3.leg1
  N4: U1.GND, LED2.cathode, LED3.cathode, R3.leg2
  N5: U1.A0, R3.wiper
  N6: R1.Pin_0, LED2.anode
  N7: R2.Pin_0, LED3.anode

custom parts:
  NodeMCU V1.0: ESP8266 based NodeMCU
